# Fritzing sketch EnerginoTwo (saved by Fritzing 0.8.3b)
circuit board: 6.88561cm x 5.36311cm
breadboards: 1

parts:
  100k = Resistor [tolerance=±5% resistance=100k package=THT]
  10k = Resistor [tolerance=±5% resistance=10k package=THT]
  1k = Resistor [tolerance=±5% resistance=1k package=THT]
  10k_2 = Resistor [tolerance=±5% resistance=10k package=THT]
  OMRON_G6E-134PL-ST-US = IC, DIP package, 12 pins [chip_label=IC spacing=300mil part_number="Omron G6E-134PL-ST-US"]
  0_1uF = Ceramic Capacitor [capacitance=0.1µF package="100 mil [THT, multilayer]"]
  1k_2 = Resistor [tolerance=±5% resistance=1k package=THT]
  47k = Resistor [tolerance=±5% resistance=47k package=THT]
  47k_2 = Resistor [tolerance=±5% resistance=47k package=THT]
  15k = Resistor [tolerance=±5% resistance=15k package=THT]
  0_1uF_2 = Ceramic Capacitor [capacitance=0.1µF package="100 mil [THT, multilayer]"]
  0_1uF_3 = Ceramic Capacitor [capacitance=0.1µF package="100 mil [THT, multilayer]"]
  0_1uF_4 = Ceramic Capacitor [capacitance=0.1µF package="100 mil [THT, multilayer]"]
  1nF = Ceramic Capacitor [capacitance=1nF package="100 mil [THT, multilayer]"]
  -IN+ = double row male pin header, 2 pins [form="♂ (male)"]
  -OUT+ = double row male pin header, 2 pins [form="♂ (male)"]
  Q1 = NPN-Transistor [package="TO92 [THT]"]
  ACS712 = ACS712 [package=so08]
  OPA344 = OPA344 [package=sot23-5]
  Energino_v2 = Arduino Uno (Rev3)

nets:
  N1: 100k.Pin_0, 10k.Pin_1, Energino_v2.A1
  N2: 100k.Pin_1, OMRON_G6E-134PL-ST-US.pin10, -IN+.pin1
  GND: 10k.Pin_0, 10k_2.Pin_0, 0_1uF.1, 47k_2.Pin_0, 0_1uF_2.1, 0_1uF_3.1, 1nF.0, -IN+.pin2, -OUT+.pin2, Q1.E, ACS712.GND, OPA344.V-, Energino_v2.GND
  N3: 1k.Pin_0, 10k_2.Pin_1, Q1.B
  N4: 1k.Pin_1, Energino_v2.D2
  N5: OMRON_G6E-134PL-ST-US.pin1, Q1.C
  5V: OMRON_G6E-134PL-ST-US.pin6, 0_1uF.0, 47k.Pin_0, 0_1uF_3.0, ACS712.VCC, OPA344.V+, Energino_v2.5V
  N6: OMRON_G6E-134PL-ST-US.pin7, ACS712.IP+
  N7: 1k_2.Pin_0, 15k.Pin_1, 0_1uF_4.1, OPA344.-IN
  N8: 1k_2.Pin_1, ACS712.VOUT
  N9: 47k.Pin_1, 47k_2.Pin_1, 0_1uF_2.0, OPA344.+IN
  N10: 15k.Pin_0, 0_1uF_4.0, OPA344.OUT, Energino_v2.A0
  N11: 1nF.1, ACS712.FILT
  N12: -OUT+.pin1, ACS712.IP-
